// Digital circuit canis.dig as structural Verilog
module canis (
  input  clk
);

  wire [15:0] add_1_s, PC_q;

  Register #(.generic("this.Bits=int(args.bits);")) PC (.D(add_1_s), .C(clk), .en(1'b1), .Q(PC_q));
  Add #(.Bits(16)) add_1 (.a(PC_q), .b(16'h1), .c_i(1'b0), .s(add_1_s));  // open: c_o
  // addressSpace addressspace_1: pin names not known; wires that end beside it: add_1_s, clk
  RegisterFile #(.AddrBits(5), .Bits(16)) Registers ();  // open: Din, we, Rw, C, Ra, Rb, Da, Db
  alu alu_1 ();  // open: a, b, op, C, out, cry
endmodule
